// Logisim project Wv1.circ as structural Verilog: 3 circuits, main circuit main
module main (
  input  in_1,
  input  in_2,
  input  in_3,
  input  [3:0] in_4,
  input  [3:0] in_5,
  input  [3:0] in_6,
  output out_7,
  output out_8
);

  wire [3:0] add_4_1_soma;

  Add_1 add_1_1 (.S(out_8), .Vai_1(out_7), .A(in_1), .B(in_2), .Vem_1(in_3));
  Add_4 add_4_1 (.B(in_5), .A(in_4), .SOMA(add_4_1_soma));  // open: Overflow
endmodule

module Add_1 (
  input  A,
  input  B,
  input  Vem_1,
  output S,
  output Vai_1
);

  wire and_1_out, and_2_out, or_1_out, xor_1_out;

  xor xor_1 (xor_1_out, B, A);
  or or_1 (or_1_out, Vem_1, B);
  and and_1 (and_1_out, B, Vem_1);
  xor xor_2 (S, Vem_1, xor_1_out);
  and and_2 (and_2_out, or_1_out, A);
  or or_2 (Vai_1, and_2_out, and_1_out);
endmodule

module Add_4 (
  input  [3:0] B,
  input  [3:0] A,
  output Overflow,
  output [3:0] SOMA
);

  wire add_1_1_vai_1, add_1_3_vai_1, add_1_4_vai_1;

  Add_1 add_1_1 (.S(SOMA[2]), .Vai_1(add_1_1_vai_1), .A(A[2]), .B(B[2]), .Vem_1(add_1_3_vai_1));
  Add_1 add_1_2 (.S(SOMA[3]), .Vai_1(Overflow), .A(A[3]), .B(B[3]), .Vem_1(add_1_1_vai_1));
  Add_1 add_1_3 (.S(SOMA[1]), .Vai_1(add_1_3_vai_1), .A(A[1]), .B(B[1]), .Vem_1(add_1_4_vai_1));
  Add_1 add_1_4 (.S(SOMA[0]), .Vai_1(add_1_4_vai_1), .A(A[0]), .B(B[0]), .Vem_1(1'b0));
endmodule
